# Fritzing sketch BIGGOD_for_print (saved by Fritzing 0.9.2b)
breadboards: 1

parts:
  Raspberry_Pi1 = Raspberry Pi 2
  fire_sensor = NPN-Transistor [package="TO92 [THT]"]
  DHT11 = NPN-Transistor [package="TO92 [THT]"]
  gas_sensor = NPN-Transistor [package="TO92 [THT]"]
  body_infrared_sensor = NPN-Transistor [package="TO92 [THT]"]

nets:
  N1: Raspberry_Pi1.GPIO25, body_infrared_sensor.B
  N2: Raspberry_Pi1.GPIO24, gas_sensor.E
  N3: Raspberry_Pi1.GPIO23, fire_sensor.C
  N4: Raspberry_Pi1.GPIO18, DHT11.B
  N5: Raspberry_Pi1.GND, fire_sensor.E, DHT11.E, gas_sensor.B, body_infrared_sensor.E
  N6: Raspberry_Pi1.5V, fire_sensor.B, DHT11.C, gas_sensor.C, body_infrared_sensor.C

notes:
  DHT11
  fire sensor
  gas sensor
  body infrared sensor
