# Fritzing sketch control_for_print (saved by Fritzing 0.9.2b)
circuit board: 8.46667cm x 5.64444cm
breadboards: 1

parts:
  Raspberry_Pi1 = Raspberry Pi 2
  Q1 = PNP-Transistor [package="TO92 [THT]"]
  Q2 = PNP-Transistor [package="TO92 [THT]"]
  Q3 = PNP-Transistor [package="TO92 [THT]"]
  C1 = Ceramic Capacitor [capacitance=100nF package="100 mil [THT, multilayer]"]

nets:
  N1: Raspberry_Pi1.GPIO16, Q2.E
  N2: Raspberry_Pi1.GND, Q1.C, Q3.E, C1.1
  N3: Raspberry_Pi1.GPIO12, Q2.B
  N4: Raspberry_Pi1.GPIO25, Q2.C
  N5: Raspberry_Pi1.GPIO23, Q3.C
  N6: Raspberry_Pi1.GPIO18, Q1.E
  N7: Raspberry_Pi1.5V, Q1.B, Q3.B, C1.0

notes:
  jidianqi
  [pwm]
  [hongwai
