# Fritzing sketch sensor_for_print (saved by Fritzing 0.9.2b)
circuit board: 8.46667cm x 5.64444cm
breadboards: 1

parts:
  fire_sensor = NPN-Transistor [package="TO92 [THT]"]
  DHT11 = NPN-Transistor [package="TO92 [THT]"]
  gas_sensor = NPN-Transistor [package="TO92 [THT]"]
  body_infrared_sensor = NPN-Transistor [package="TO92 [THT]"]
  Raspberry_Pi1 = Raspberry Pi 2

nets:
  N1: fire_sensor.E, DHT11.E, gas_sensor.B, body_infrared_sensor.E, Raspberry_Pi1.GND
  N2: fire_sensor.B, DHT11.C, gas_sensor.C, body_infrared_sensor.C, Raspberry_Pi1.5V
  N3: fire_sensor.C, Raspberry_Pi1.GPIO23
  N4: DHT11.B, Raspberry_Pi1.GPIO18
  N5: gas_sensor.E, Raspberry_Pi1.GPIO24
  N6: body_infrared_sensor.B, Raspberry_Pi1.GPIO25

notes:
  DHT11
  fire sensor
  gas sensor
  body infrared sensor
