# Fritzing sketch 超声1602 (saved by Fritzing 0.9.2b)
circuit board: 9.90787cm x 6.28979cm
breadboards: 1

parts:
  LCD1 = LCD screen
  Raspberry_Pi1 = Raspberry Pi 2
  元件1 = SRF05 Ultrasonic Rangefinder  # not connected

nets:
  VSS: LCD1.VSS, LCD1.V0, LCD1.R/W, LCD1.LED-, Raspberry_Pi1.GND
  VDD: LCD1.VDD, LCD1.LED+, Raspberry_Pi1.5V
  N1: LCD1.RS, Raspberry_Pi1.GPIO7
  N2: LCD1.E, Raspberry_Pi1.GPIO8
  N3: LCD1.DB0, Raspberry_Pi1.GPIO17
  N4: LCD1.DB1, Raspberry_Pi1.GPIO18
  N5: LCD1.DB2, Raspberry_Pi1.GPIO27
  N6: LCD1.DB3, Raspberry_Pi1.GPIO22
  N7: LCD1.DB4, Raspberry_Pi1.GPIO23
  N8: LCD1.DB5, Raspberry_Pi1.GPIO24
  N9: LCD1.DB6, Raspberry_Pi1.GPIO25
  N10: LCD1.DB7, Raspberry_Pi1.GPIO4
